// Logisim project qualquerSequencia.circ as structural Verilog: 1 circuit, main circuit main
module main (
);

  wire clock_1_out, clock_2_out, clock_3_out, or_1_out, q3_qn;
  wire [3:0] q0_2_q, q0_3_q, q0_q;

  Clock clock_1 (.out(clock_1_out));
  Clock clock_2 (.out(clock_2_out));
  Clock clock_3 (.out(clock_3_out));
  J_K_Flip_Flop q3 (
    .J(q0_2_q[0]), .clk(clock_2_out), .K(q0_2_q[1]), .Q(q0_2_q[3]), .Qn(q3_qn));  // open: preset, en, reset
  J_K_Flip_Flop q3_2 (.J(q0_3_q[2]), .clk(clock_3_out), .K(1'b1), .Q(q0_3_q[3]));  // open: Qn, preset, en, reset
  J_K_Flip_Flop q3_3 (.J(q0_q[0]), .clk(clock_1_out), .K(1'b1), .Q(q0_q[3]));  // open: Qn, preset, en, reset
  or or_1 (or_1_out, q0_q[3], q0_q[1]);
  J_K_Flip_Flop q2 (.J(1'b1), .clk(clock_1_out), .K(or_1_out), .Q(q0_q[2]));  // open: Qn, preset, en, reset
  J_K_Flip_Flop q2_2 (.J(q3_qn), .clk(clock_2_out), .K(q0_2_q[3]), .Q(q0_2_q[2]));  // open: Qn, preset, en, reset
  J_K_Flip_Flop q2_3 (.J(q0_3_q[1]), .clk(clock_3_out), .K(1'b1), .Q(q0_3_q[2]));  // open: Qn, preset, en, reset
  J_K_Flip_Flop q1 (.J(q0_q[3]), .clk(clock_1_out), .K(q0_q[3]), .Q(q0_q[1]));  // open: Qn, preset, en, reset
  J_K_Flip_Flop q1_2 (.J(1'b1), .clk(clock_2_out), .K(q0_2_q[2]), .Q(q0_2_q[1]));  // open: Qn, preset, en, reset
  J_K_Flip_Flop q1_3 (.J(q0_3_q[0]), .clk(clock_3_out), .K(1'b1), .Q(q0_3_q[1]));  // open: Qn, preset, en, reset
  J_K_Flip_Flop q0 (.J(q0_q[1]), .clk(clock_1_out), .K(1'b1), .Q(q0_q[0]));  // open: Qn, preset, en, reset
  J_K_Flip_Flop q0_2 (.J(q3_qn), .clk(clock_2_out), .K(q0_2_q[3]), .Q(q0_2_q[0]));  // open: Qn, preset, en, reset
  J_K_Flip_Flop q0_3 (.J(q0_3_q[3]), .clk(clock_3_out), .K(1'b1), .Q(q0_3_q[0]));  // open: Qn, preset, en, reset
  Hex_Digit_Display hex_digit_display_1 (.value(q0_q));  // open: dp
  Hex_Digit_Display hex_digit_display_2 (.value(q0_2_q));  // open: dp
  Hex_Digit_Display hex_digit_display_3 (.value(q0_3_q));  // open: dp
endmodule
