// Logisim project ula.circ as structural Verilog: 8 circuits, main circuit main
module main (
  input  [7:0] A,
  input  [7:0] B,
  input  [2:0] Operation,
  output [15:0] S
);

  wire op1, op2, op3, op4, op5, op6, op7, op8, undriven, undriven_2, undriven_3;
  wire [7:0] and_1_out, divisao_1_quociente, divisao_2_resto, lockahead_1_s, lockahead_2_s, not_1_out,
       not_2_out, or_1_out, undriven_4, undriven_5, undriven_6, undriven_7, undriven_8, undriven_9;
  wire [15:0] multiplicacao_1_out_3, undriven_10;

  assign and_1_out = A & B;  // AND_Gate and_1, 8 bits wide
  assign or_1_out = A | B;  // OR_Gate or_1, 8 bits wide
  lockahead lockahead_1 (.A(A), .B(B), .Op(1'b0), .S(lockahead_1_s));  // open: Bit, out_6
  lockahead lockahead_2 (.A(A), .B(B), .Op(1'b1), .S(lockahead_2_s));  // open: Bit, out_6
  divisao divisao_1 (.Dividendo(A), .Divisor(B), .Quociente(divisao_1_quociente));  // open: Resto
  divisao divisao_2 (.Dividendo(A), .Divisor(B), .Resto(divisao_2_resto));  // open: Quociente
  multiplicacao multiplicacao_1 (.in_1(A), .in_2(B), .out_3(multiplicacao_1_out_3));
  assign not_1_out = ~A;  // NOT_Gate not_1, 8 bits wide
  Multiplexer #(.select(3), .width(16), .enable("false")) multiplexer_1 (
    .in0({{8{1'b0}}, and_1_out}), .in1({{8{1'b0}}, or_1_out}), .in2({{8{1'b0}}, not_1_out}),
    .in3({{8{1'b0}}, lockahead_1_s}), .in4({{8{1'b0}}, lockahead_2_s}),
    .in5({{8{1'b0}}, divisao_1_quociente}), .in6({{8{1'b0}}, divisao_2_resto}), .in7(multiplicacao_1_out_3),
    .out(S), .sel(Operation));
  and and_2 (op1, ~undriven_2, ~undriven, ~undriven_3);  // AND_Gate
  and and_3 (op2, ~undriven_2, ~undriven, undriven_3);  // AND_Gate
  and and_4 (op3, ~undriven_2, undriven, ~undriven_3);  // AND_Gate
  and and_5 (op4, ~undriven_2, undriven, undriven_3);  // AND_Gate
  and and_6 (op5, undriven_2, ~undriven, ~undriven_3);  // AND_Gate
  and and_7 (op6, undriven_2, ~undriven, undriven_3);  // AND_Gate
  and and_8 (op7, undriven_2, undriven, ~undriven_3);  // AND_Gate
  and and_9 (op8, undriven_2, undriven, undriven_3);
  // NOT_Gate not_2 has open pins: in=open, out=not_2_out
  Multiplexer #(.width(8), .enable("false")) multiplexer_2 (.in0({8{1'b0}}), .in1(undriven_4), .sel(op1));  // open: out
  Multiplexer #(.width(8), .enable("false")) multiplexer_3 (.in0({8{1'b0}}), .in1(undriven_5), .sel(op2));  // open: out
  Multiplexer #(.width(8), .enable("false")) multiplexer_4 (.in0({8{1'b0}}), .in1(not_2_out), .sel(op3));  // open: out
  Multiplexer #(.width(8), .enable("false")) multiplexer_5 (.in0({8{1'b0}}), .in1(undriven_6), .sel(op4));  // open: out
  Multiplexer #(.width(8), .enable("false")) multiplexer_6 (.in0({8{1'b0}}), .in1(undriven_7), .sel(op5));  // open: out
  Multiplexer #(.width(8), .enable("false")) multiplexer_7 (.in0({8{1'b0}}), .in1(undriven_8), .sel(op6));  // open: out
  Multiplexer #(.width(8), .enable("false")) multiplexer_8 (.in0({8{1'b0}}), .in1(undriven_9), .sel(op7));  // open: out
  Multiplexer #(.width(16), .enable("false")) multiplexer_9 (
    .in0({16{1'b0}}), .in1(undriven_10), .sel(op8));  // open: out
endmodule

module lockahead (
  input  [7:0] A,
  input  [7:0] B,
  input  Op,
  output [7:0] S,
  output Bit,
  output out_6
);

  wire and_1_out, and_2_out, and_3_out, and_4_out, and_5_out, and_6_out, and_7_out, and_8_out, and_9_out,
       and_10_out, and_11_out, and_12_out, and_13_out, and_14_out, and_15_out, and_16_out, and_17_out,
       and_18_out, and_19_out, and_20_out, and_21_out, and_22_out, and_23_out, and_24_out, and_25_out,
       and_26_out, and_27_out, and_28_out, and_29_out, and_30_out, and_31_out, and_32_out, and_33_out,
       and_34_out, and_35_out, and_36_out, G7_out, or_1_out, or_3_out, or_4_out, or_5_out, or_6_out,
       or_7_out, or_8_out, or_9_out, P0_out, P1_out, P2_out, P3_out, P4_out, P5_out, P6_out, P7_out;
  wire [6:0] G0_out;
  wire [7:0] xor_1_out;

  and and_1 (and_1_out, Op, Op, P0_out, P1_out, P2_out, P4_out, P5_out, P6_out, P7_out);
  and and_2 (and_2_out, G0_out[0], P0_out, P1_out, P2_out, P4_out, P5_out, P6_out, P7_out);
  and and_3 (and_3_out, G0_out[1], P1_out, P2_out, P4_out, P5_out, P6_out, P7_out);
  and and_4 (and_4_out, G0_out[2], P2_out, P4_out, P5_out, P6_out, P7_out);
  and and_5 (and_5_out, G0_out[3], P2_out, P4_out, P6_out, P7_out);
  and and_6 (and_6_out, G0_out[4], P4_out, P5_out, P7_out);
  and and_7 (and_7_out, G0_out[5], P6_out, P7_out);
  and and_8 (and_8_out, G0_out[6], P7_out);
  or or_1 (or_1_out, and_1_out, and_2_out, and_3_out, and_4_out, and_5_out, and_6_out, and_7_out, and_8_out);
  or or_2 (out_6, or_1_out, G7_out);
  assign xor_1_out = B ^ {8{Op}};  // XOR_Gate xor_1, 8 bits wide
  or P7 (P7_out, xor_1_out[7], xor_1_out[7]);
  and G7 (G7_out, xor_1_out[7], xor_1_out[7]);
  and and_9 (and_9_out, Op, P0_out, P1_out, P2_out, P3_out, P4_out, P5_out, P6_out);
  mainLockahead mainlockahead_1 (.S(Bit), .A(xor_1_out[7]), .B(A[7]), .Cin(or_3_out));
  and and_10 (and_10_out, P6_out, P5_out, P4_out, P3_out, P2_out, P1_out, G0_out[0]);
  or or_3 (or_3_out, and_9_out, and_10_out, and_11_out, and_12_out, and_13_out, and_14_out, and_15_out, G0_out[6]);
  and and_11 (and_11_out, P6_out, P5_out, P4_out, P3_out, P2_out, G0_out[1]);
  and and_12 (and_12_out, P6_out, P5_out, P4_out, P3_out, G0_out[2]);
  and and_13 (and_13_out, P6_out, P5_out, P4_out, G0_out[3]);
  and and_14 (and_14_out, P6_out, P5_out, G0_out[4]);
  and and_15 (and_15_out, P6_out, G0_out[5]);
  or P6 (P6_out, xor_1_out[6], A[6]);
  and G6 (G0_out[6], xor_1_out[6], A[6]);
  and and_16 (and_16_out, Op, P0_out, P1_out, P2_out, P3_out, P4_out, P5_out);
  mainLockahead mainlockahead_2 (.S(S[6]), .A(A[6]), .B(xor_1_out[6]), .Cin(or_4_out));
  and and_17 (and_17_out, P5_out, P4_out, P3_out, P2_out, P1_out, G0_out[0]);
  or or_4 (or_4_out, and_16_out, and_17_out, and_18_out, and_19_out, and_20_out, and_21_out, G0_out[5]);
  and and_18 (and_18_out, P5_out, P4_out, P3_out, P2_out, G0_out[1]);
  and and_19 (and_19_out, P5_out, P4_out, P3_out, G0_out[2]);
  and and_20 (and_20_out, P4_out, P5_out, G0_out[3]);
  or P5 (P5_out, xor_1_out[5], A[5]);
  and G5 (G0_out[5], xor_1_out[5], A[5]);
  and and_21 (and_21_out, P5_out, G0_out[4]);
  and and_22 (and_22_out, Op, P0_out, P1_out, P2_out, P3_out, P4_out);
  or or_5 (or_5_out, and_22_out, and_23_out, and_24_out, and_25_out, and_26_out, G0_out[4]);
  mainLockahead mainlockahead_3 (.S(S[5]), .A(A[5]), .B(xor_1_out[5]), .Cin(or_5_out));
  and and_23 (and_23_out, P4_out, P3_out, P2_out, P1_out, G0_out[0]);
  and and_24 (and_24_out, P4_out, P3_out, P2_out, G0_out[1]);
  and and_25 (and_25_out, P4_out, P3_out, G0_out[2]);
  or P4 (P4_out, xor_1_out[4], A[4]);
  and G4 (G0_out[4], xor_1_out[4], A[4]);
  and and_26 (and_26_out, P4_out, G0_out[3]);
  and and_27 (and_27_out, Op, P0_out, P1_out, P2_out, P3_out);
  mainLockahead mainlockahead_4 (.S(S[4]), .A(A[4]), .B(xor_1_out[4]), .Cin(or_6_out));
  and and_28 (and_28_out, P3_out, P2_out, P1_out, G0_out[0]);
  or or_6 (or_6_out, and_27_out, and_28_out, and_30_out, and_29_out, G0_out[3]);
  or P3 (P3_out, xor_1_out[3], A[3]);
  and G3 (G0_out[3], xor_1_out[3], A[3]);
  and and_29 (and_29_out, P3_out, G0_out[2]);
  and and_30 (and_30_out, P3_out, P2_out, G0_out[1]);
  and and_31 (and_31_out, Op, P0_out, P1_out, P2_out);
  and and_32 (and_32_out, P2_out, P1_out, G0_out[0]);
  or or_7 (or_7_out, and_31_out, and_32_out, and_33_out, G0_out[2]);
  mainLockahead mainlockahead_5 (.S(S[3]), .A(A[3]), .B(xor_1_out[3]), .Cin(or_7_out));
  or P2 (P2_out, xor_1_out[2], A[2]);
  and G2 (G0_out[2], xor_1_out[2], A[2]);
  and and_33 (and_33_out, P2_out, G0_out[1]);
  and and_34 (and_34_out, P0_out, P1_out, Op);
  or or_8 (or_8_out, and_34_out, and_35_out, G0_out[1]);
  mainLockahead mainlockahead_6 (.S(S[2]), .A(A[2]), .B(xor_1_out[2]), .Cin(or_8_out));
  or P1 (P1_out, xor_1_out[1], A[1]);
  and G1 (G0_out[1], xor_1_out[1], A[1]);
  and and_35 (and_35_out, P1_out, G0_out[0]);
  mainLockahead mainlockahead_7 (.S(S[1]), .A(A[1]), .B(xor_1_out[1]), .Cin(or_9_out));
  or P0 (P0_out, xor_1_out[0], A[0]);
  and G0 (G0_out[0], xor_1_out[0], A[0]);
  and and_36 (and_36_out, P0_out, Op);
  or or_9 (or_9_out, and_36_out, G0_out[0]);
  mainLockahead mainlockahead_8 (.S(S[0]), .A(A[0]), .B(xor_1_out[0]), .Cin(Op));

  assign S[7] = Bit;
endmodule

module mainLockahead (
  input  A,
  input  B,
  input  Cin,
  output S
);

  wire xor_1_out;

  xor xor_1 (xor_1_out, B, A);
  xor xor_2 (S, xor_1_out, Cin);
endmodule

module divisao (
  input  [7:0] Dividendo,
  input  [7:0] Divisor,
  output [7:0] Quociente,
  output [7:0] Resto
);

  wire lockahead_1_bit, lockahead_2_bit, lockahead_3_bit, lockahead_4_bit, lockahead_5_bit, lockahead_6_bit,
       lockahead_7_bit, lockahead_8_bit;
  wire [7:0] lockahead_1_s, lockahead_2_s, lockahead_3_s, lockahead_4_s, lockahead_5_s, lockahead_6_s,
       lockahead_7_s, lockahead_8_s, multiplexer_1_out, multiplexer_2_out, multiplexer_4_out,
       multiplexer_5_out, multiplexer_6_out, multiplexer_7_out;
  wire [7:1] multiplexer_3_out_2;
  wire [7:7] multiplexer_3_out;

  lockahead lockahead_1 (
    .A({{7{1'b0}}, Dividendo[7]}), .B(Divisor), .Op(1'b1), .S(lockahead_1_s), .Bit(lockahead_1_bit));  // open: out_6
  not not_1 (Quociente[7], lockahead_1_bit);
  Multiplexer #(.width(8), .enable("false")) multiplexer_1 (
    .in0(lockahead_1_s), .in1({{7{1'b0}}, Dividendo[7]}), .out(multiplexer_1_out), .sel(lockahead_1_bit));
  not not_2 (Quociente[6], lockahead_2_bit);
  lockahead lockahead_2 (
    .A({multiplexer_1_out[6:0], Dividendo[6]}), .B(Divisor), .Op(1'b1), .S(lockahead_2_s),
    .Bit(lockahead_2_bit));  // open: out_6
  Multiplexer #(.width(8), .enable("false")) multiplexer_2 (
    .in0(lockahead_2_s), .in1({multiplexer_1_out[6:0], Dividendo[6]}), .out(multiplexer_2_out),
    .sel(lockahead_2_bit));
  lockahead lockahead_3 (
    .A({multiplexer_2_out[6:0], Dividendo[5]}), .B(Divisor), .Op(1'b1), .S(lockahead_3_s),
    .Bit(lockahead_3_bit));  // open: out_6
  not not_3 (Quociente[5], lockahead_3_bit);
  Multiplexer #(.width(8), .enable("false")) multiplexer_3 (
    .in0(lockahead_3_s), .in1({multiplexer_2_out[6:0], Dividendo[5]}),
    .out({multiplexer_3_out[7], multiplexer_3_out_2}), .sel(lockahead_3_bit));
  lockahead lockahead_4 (
    .A({multiplexer_3_out_2, Dividendo[4]}), .B(Divisor), .Op(1'b1), .S(lockahead_4_s), .Bit(lockahead_4_bit));  // open: out_6
  not not_4 (Quociente[4], lockahead_4_bit);
  Multiplexer #(.width(8), .enable("false")) multiplexer_4 (
    .in0(lockahead_4_s), .in1({multiplexer_3_out_2, Dividendo[4]}), .out(multiplexer_4_out),
    .sel(lockahead_4_bit));
  lockahead lockahead_5 (
    .A({multiplexer_4_out[6:0], Dividendo[3]}), .B(Divisor), .Op(1'b1), .S(lockahead_5_s),
    .Bit(lockahead_5_bit));  // open: out_6
  not not_5 (Quociente[3], lockahead_5_bit);
  Multiplexer #(.width(8), .enable("false")) multiplexer_5 (
    .in0(lockahead_5_s), .in1({multiplexer_4_out[6:0], Dividendo[3]}), .out(multiplexer_5_out),
    .sel(lockahead_5_bit));
  not not_6 (Quociente[2], lockahead_6_bit);
  lockahead lockahead_6 (
    .A({multiplexer_5_out[6:0], Dividendo[2]}), .B(Divisor), .Op(1'b1), .S(lockahead_6_s),
    .Bit(lockahead_6_bit));  // open: out_6
  Multiplexer #(.width(8), .enable("false")) multiplexer_6 (
    .in0(lockahead_6_s), .in1({multiplexer_5_out[6:0], Dividendo[2]}), .out(multiplexer_6_out),
    .sel(lockahead_6_bit));
  lockahead lockahead_7 (
    .A({multiplexer_6_out[6:0], Dividendo[1]}), .B(Divisor), .Op(1'b1), .S(lockahead_7_s),
    .Bit(lockahead_7_bit));  // open: out_6
  not not_7 (Quociente[1], lockahead_7_bit);
  Multiplexer #(.width(8), .enable("false")) multiplexer_7 (
    .in0(lockahead_7_s), .in1({multiplexer_6_out[6:0], Dividendo[1]}), .out(multiplexer_7_out),
    .sel(lockahead_7_bit));
  lockahead lockahead_8 (
    .A({multiplexer_7_out[6:0], Dividendo[0]}), .B(Divisor), .Op(1'b1), .S(lockahead_8_s),
    .Bit(lockahead_8_bit));  // open: out_6
  not not_8 (Quociente[0], lockahead_8_bit);
  Multiplexer #(.width(8), .enable("false")) multiplexer_8 (
    .in0(lockahead_8_s), .in1({multiplexer_7_out[6:0], Dividendo[0]}), .out(Resto), .sel(lockahead_8_bit));

  // Other names for the same wires on the sheet: D[7:0] = Dividendo; Div[7:0] = Divisor; S7 = Quociente[0];
  //   S6 = Quociente[1]; S5 = Quociente[2]; S4 = Quociente[3]; S3 = Quociente[4]; S2 = Quociente[5];
  //   S1 = Quociente[6]; S0 = Quociente[7]
endmodule

module multiplicacao (
  input  [7:0] in_1,
  input  [7:0] in_2,
  output [15:0] out_3
);

  wire _1_2, _1_3, _1_4, _1_5, _1_6, _1_7, _1_8, _2_1, _2_2, _2_3, _2_4, _2_5, _2_6, _2_7, _2_8, _3_1, _3_2,
       _3_3, _3_4, _3_5, _3_6, _3_7, _3_8, _4_1, _4_2, _4_3, _4_4, _4_5, _4_6, _4_7, _4_8, _5_1, _5_2, _5_3,
       _5_4, _5_5, _5_6, _5_7, _5_8, _6_1, _6_2, _6_3, _6_4, _6_5, _6_6, _6_7, _6_8, _7_1, _7_2, _7_3, _7_4,
       _7_5, _7_6, _7_7, _7_8, _8_1, _8_2, _8_3, _8_4, _8_5, _8_6, _8_7, _8_8, sumtomult_2_1_cout,
       sumtomult_2_1_s, sumtomult_2_2_cout, sumtomult_2_3_cout, sumtomult_2_4_cout, sumtomult_2_5_cout,
       sumtomult_2_6_cout, sumtomult_2_7_cout, sumtomult_2_8_cout, sumtomult_2_cout, sumtomult_2_s,
       sumtomult_3_cout, sumtomult_3_s, sumtomult_4_cout, sumtomult_4_s, sumtomult_5_cout, sumtomult_6_cout,
       sumtomult_7_cout, sumtomult_7_s, sumtomult_8_cout, sumtomult_8_s, sumtomult_9_cout, sumtomult_9_s,
       sumtomult_10_cout, sumtomult_11_cout, sumtomult_11_s, sumtomult_12_cout, sumtomult_12_s,
       sumtomult_13_cout, sumtomult_13_s, sumtomult_14_cout, sumtomult_14_s, sumtomult_15_cout,
       sumtomult_15_s, sumtomult_16_cout, sumtomult_16_s, sumtomult_17_cout, sumtomult_17_s,
       sumtomult_18_cout, sumtomult_18_s, sumtomult_19_cout, sumtomult_19_s, sumtomult_20_cout,
       sumtomult_21_cout, sumtomult_22_cout, sumtomult_22_s, sumtomult_23_cout, sumtomult_23_s,
       sumtomult_24_cout, sumtomult_24_s, sumtomult_25_cout, sumtomult_25_s, sumtomult_26_cout,
       sumtomult_26_s, sumtomult_27_cout, sumtomult_27_s, sumtomult_28_cout, sumtomult_28_s,
       sumtomult_29_cout, sumtomult_29_s, sumtomult_30_cout, sumtomult_30_s, sumtomult_31_cout,
       sumtomult_31_s, sumtomult_32_cout, sumtomult_32_s, sumtomult_33_cout, sumtomult_34_cout,
       sumtomult_34_s, sumtomult_35_cout, sumtomult_35_s, sumtomult_36_cout, sumtomult_36_s,
       sumtomult_37_cout, sumtomult_37_s, sumtomult_38_cout, sumtomult_38_s, sumtomult_39_cout,
       sumtomult_39_s, sumtomult_40_cout, sumtomult_40_s, sumtomult_41_cout, sumtomult_41_s,
       sumtomult_42_cout, sumtomult_42_s, sumtomult_43_cout, sumtomult_43_s, sumtomult_44_cout,
       sumtomult_44_s, sumtomult_45_cout, sumtomult_45_s, sumtomult_46_cout, sumtomult_46_s,
       sumtomult_47_cout, sumtomult_47_s, sumtomult_48_cout, sumtomult_48_s;

  SumToMult sumtomult_1 (.Cout(out_3[15]), .S(out_3[14]), .A(sumtomult_3_cout), .B(_8_8), .C(sumtomult_6_cout));
  SumToMult sumtomult_2 (
    .Cout(sumtomult_2_cout), .S(sumtomult_2_s), .A(sumtomult_7_cout), .B(_8_6), .C(sumtomult_8_cout));
  SumToMult sumtomult_3 (
    .Cout(sumtomult_3_cout), .S(sumtomult_3_s), .A(sumtomult_2_cout), .B(_8_7), .C(sumtomult_4_cout));
  SumToMult sumtomult_4 (.Cout(sumtomult_4_cout), .S(sumtomult_4_s), .A(sumtomult_2_s), .B(_7_7), .C(sumtomult_9_cout));
  SumToMult sumtomult_5 (.Cout(sumtomult_5_cout), .S(out_3[12]), .A(sumtomult_4_s), .B(_6_8), .C(sumtomult_10_cout));
  SumToMult sumtomult_6 (.Cout(sumtomult_6_cout), .S(out_3[13]), .A(sumtomult_3_s), .B(_7_8), .C(sumtomult_5_cout));
  SumToMult sumtomult_7 (
    .Cout(sumtomult_7_cout), .S(sumtomult_7_s), .A(sumtomult_12_cout), .B(_8_5), .C(sumtomult_15_cout));
  SumToMult sumtomult_8 (
    .Cout(sumtomult_8_cout), .S(sumtomult_8_s), .A(sumtomult_7_s), .B(_7_6), .C(sumtomult_16_cout));
  SumToMult sumtomult_9 (
    .Cout(sumtomult_9_cout), .S(sumtomult_9_s), .A(sumtomult_8_s), .B(_6_7), .C(sumtomult_19_cout));
  SumToMult sumtomult_10 (.Cout(sumtomult_10_cout), .S(out_3[11]), .A(sumtomult_9_s), .B(_5_8), .C(sumtomult_20_cout));
  SumToMult_2 sumtomult_2_1 (.A(_8_2), .S(sumtomult_2_1_s), .B(sumtomult_22_cout), .Cout(sumtomult_2_1_cout));
  SumToMult sumtomult_11 (
    .Cout(sumtomult_11_cout), .S(sumtomult_11_s), .A(sumtomult_2_1_cout), .B(_8_3), .C(sumtomult_23_cout));
  SumToMult sumtomult_12 (
    .Cout(sumtomult_12_cout), .S(sumtomult_12_s), .A(sumtomult_11_cout), .B(_8_4), .C(sumtomult_13_cout));
  SumToMult sumtomult_13 (
    .Cout(sumtomult_13_cout), .S(sumtomult_13_s), .A(sumtomult_11_s), .B(_7_4), .C(sumtomult_26_cout));
  SumToMult sumtomult_14 (
    .Cout(sumtomult_14_cout), .S(sumtomult_14_s), .A(sumtomult_13_s), .B(_6_5), .C(sumtomult_28_cout));
  SumToMult sumtomult_15 (
    .Cout(sumtomult_15_cout), .S(sumtomult_15_s), .A(sumtomult_12_s), .B(_7_5), .C(sumtomult_14_cout));
  SumToMult sumtomult_16 (
    .Cout(sumtomult_16_cout), .S(sumtomult_16_s), .A(sumtomult_15_s), .B(_6_6), .C(sumtomult_17_cout));
  SumToMult sumtomult_17 (
    .Cout(sumtomult_17_cout), .S(sumtomult_17_s), .A(sumtomult_14_s), .B(_5_6), .C(sumtomult_30_cout));
  SumToMult sumtomult_18 (
    .Cout(sumtomult_18_cout), .S(sumtomult_18_s), .A(sumtomult_17_s), .B(_4_7), .C(sumtomult_32_cout));
  SumToMult sumtomult_19 (
    .Cout(sumtomult_19_cout), .S(sumtomult_19_s), .A(sumtomult_16_s), .B(_5_7), .C(sumtomult_18_cout));
  SumToMult sumtomult_20 (.Cout(sumtomult_20_cout), .S(out_3[10]), .A(sumtomult_19_s), .B(_4_8), .C(sumtomult_21_cout));
  SumToMult sumtomult_21 (.Cout(sumtomult_21_cout), .S(out_3[9]), .A(sumtomult_18_s), .B(_3_8), .C(sumtomult_33_cout));
  SumToMult sumtomult_22 (.Cout(sumtomult_22_cout), .S(sumtomult_22_s), .A(_7_2), .B(_8_1), .C(sumtomult_34_cout));
  SumToMult sumtomult_23 (
    .Cout(sumtomult_23_cout), .S(sumtomult_23_s), .A(sumtomult_2_1_s), .B(_7_3), .C(sumtomult_24_cout));
  SumToMult sumtomult_24 (
    .Cout(sumtomult_24_cout), .S(sumtomult_24_s), .A(sumtomult_22_s), .B(_6_3), .C(sumtomult_35_cout));
  SumToMult sumtomult_25 (
    .Cout(sumtomult_25_cout), .S(sumtomult_25_s), .A(sumtomult_24_s), .B(_5_4), .C(sumtomult_36_cout));
  SumToMult sumtomult_26 (
    .Cout(sumtomult_26_cout), .S(sumtomult_26_s), .A(sumtomult_23_s), .B(_6_4), .C(sumtomult_25_cout));
  SumToMult sumtomult_27 (
    .Cout(sumtomult_27_cout), .S(sumtomult_27_s), .A(sumtomult_25_s), .B(_4_5), .C(sumtomult_37_cout));
  SumToMult sumtomult_28 (
    .Cout(sumtomult_28_cout), .S(sumtomult_28_s), .A(sumtomult_26_s), .B(_5_5), .C(sumtomult_27_cout));
  SumToMult sumtomult_29 (
    .Cout(sumtomult_29_cout), .S(sumtomult_29_s), .A(sumtomult_27_s), .B(_3_6), .C(sumtomult_38_cout));
  SumToMult sumtomult_30 (
    .Cout(sumtomult_30_cout), .S(sumtomult_30_s), .A(sumtomult_28_s), .B(_4_6), .C(sumtomult_29_cout));
  SumToMult sumtomult_31 (
    .Cout(sumtomult_31_cout), .S(sumtomult_31_s), .A(sumtomult_29_s), .B(_2_7), .C(sumtomult_2_4_cout));
  SumToMult sumtomult_32 (
    .Cout(sumtomult_32_cout), .S(sumtomult_32_s), .A(sumtomult_30_s), .B(_3_7), .C(sumtomult_31_cout));
  SumToMult_2 sumtomult_2_2 (.A(sumtomult_31_s), .S(out_3[7]), .B(_1_8), .Cout(sumtomult_2_2_cout));
  SumToMult sumtomult_33 (.Cout(sumtomult_33_cout), .S(out_3[8]), .A(sumtomult_32_s), .B(_2_8), .C(sumtomult_2_2_cout));
  SumToMult sumtomult_34 (.Cout(sumtomult_34_cout), .S(sumtomult_34_s), .A(_6_2), .B(_7_1), .C(sumtomult_39_cout));
  SumToMult sumtomult_35 (
    .Cout(sumtomult_35_cout), .S(sumtomult_35_s), .A(sumtomult_34_s), .B(_5_3), .C(sumtomult_42_cout));
  SumToMult sumtomult_36 (
    .Cout(sumtomult_36_cout), .S(sumtomult_36_s), .A(sumtomult_35_s), .B(_4_4), .C(sumtomult_44_cout));
  SumToMult sumtomult_37 (
    .Cout(sumtomult_37_cout), .S(sumtomult_37_s), .A(sumtomult_36_s), .B(_3_5), .C(sumtomult_45_cout));
  SumToMult_2 sumtomult_2_3 (.A(sumtomult_45_s), .S(out_3[5]), .B(_1_6), .Cout(sumtomult_2_3_cout));
  SumToMult sumtomult_38 (
    .Cout(sumtomult_38_cout), .S(sumtomult_38_s), .A(sumtomult_37_s), .B(_2_6), .C(sumtomult_2_3_cout));
  SumToMult_2 sumtomult_2_4 (.A(sumtomult_38_s), .S(out_3[6]), .B(_1_7), .Cout(sumtomult_2_4_cout));
  SumToMult sumtomult_39 (.Cout(sumtomult_39_cout), .S(sumtomult_39_s), .A(_5_2), .B(_6_1), .C(sumtomult_40_cout));
  SumToMult sumtomult_40 (.Cout(sumtomult_40_cout), .S(sumtomult_40_s), .A(_4_2), .B(_5_1), .C(sumtomult_46_cout));
  SumToMult sumtomult_41 (
    .Cout(sumtomult_41_cout), .S(sumtomult_41_s), .A(sumtomult_40_s), .B(_3_3), .C(sumtomult_47_cout));
  SumToMult sumtomult_42 (
    .Cout(sumtomult_42_cout), .S(sumtomult_42_s), .A(sumtomult_39_s), .B(_4_3), .C(sumtomult_41_cout));
  SumToMult_2 sumtomult_2_5 (.A(sumtomult_47_s), .S(out_3[3]), .B(_1_4), .Cout(sumtomult_2_5_cout));
  SumToMult sumtomult_43 (
    .Cout(sumtomult_43_cout), .S(sumtomult_43_s), .A(sumtomult_41_s), .B(_2_4), .C(sumtomult_2_5_cout));
  SumToMult sumtomult_44 (
    .Cout(sumtomult_44_cout), .S(sumtomult_44_s), .A(sumtomult_42_s), .B(_3_4), .C(sumtomult_43_cout));
  SumToMult sumtomult_45 (
    .Cout(sumtomult_45_cout), .S(sumtomult_45_s), .A(sumtomult_44_s), .B(_2_5), .C(sumtomult_2_6_cout));
  SumToMult_2 sumtomult_2_6 (.A(sumtomult_43_s), .S(out_3[4]), .B(_1_5), .Cout(sumtomult_2_6_cout));
  SumToMult sumtomult_46 (.Cout(sumtomult_46_cout), .S(sumtomult_46_s), .A(_3_2), .B(_4_1), .C(sumtomult_48_cout));
  SumToMult_2 sumtomult_2_7 (.A(sumtomult_48_s), .S(out_3[2]), .B(_1_3), .Cout(sumtomult_2_7_cout));
  SumToMult sumtomult_47 (
    .Cout(sumtomult_47_cout), .S(sumtomult_47_s), .A(sumtomult_46_s), .B(_2_3), .C(sumtomult_2_7_cout));
  SumToMult sumtomult_48 (.Cout(sumtomult_48_cout), .S(sumtomult_48_s), .A(_2_2), .B(_3_1), .C(sumtomult_2_8_cout));
  SumToMult_2 sumtomult_2_8 (.A(_1_2), .S(out_3[1]), .B(_2_1), .Cout(sumtomult_2_8_cout));
  and and_1 (_6_1, in_1[5], in_2[0]);
  and and_2 (_7_1, in_1[6], in_2[0]);
  and and_3 (_8_1, in_1[7], in_2[0]);
  and and_4 (_7_2, in_1[6], in_2[1]);
  and and_5 (_8_2, in_1[7], in_2[1]);
  and and_6 (_6_2, in_1[5], in_2[1]);
  and and_7 (_8_3, in_1[7], in_2[2]);
  and and_8 (_7_3, in_1[6], in_2[2]);
  and and_9 (_6_3, in_1[5], in_2[2]);
  and and_10 (_7_4, in_1[6], in_2[3]);
  and and_11 (_6_4, in_1[5], in_2[3]);
  and and_12 (_8_4, in_1[7], in_2[3]);
  and and_13 (_8_5, in_1[7], in_2[4]);
  and and_14 (_7_5, in_1[6], in_2[4]);
  and and_15 (_6_5, in_1[5], in_2[4]);
  and and_16 (_8_6, in_1[7], in_2[5]);
  and and_17 (_6_6, in_1[5], in_2[5]);
  and and_18 (_7_6, in_1[6], in_2[5]);
  and and_19 (_6_7, in_1[5], in_2[6]);
  and and_20 (_7_7, in_1[6], in_2[6]);
  and and_21 (_8_7, in_1[7], in_2[6]);
  and and_22 (_7_8, in_1[6], in_2[7]);
  and and_23 (_6_8, in_1[5], in_2[7]);
  and and_24 (_8_8, in_1[7], in_2[7]);
  and and_25 (_4_1, in_1[3], in_2[0]);
  and and_26 (_5_1, in_1[4], in_2[0]);
  and and_27 (_5_2, in_1[4], in_2[1]);
  and and_28 (_4_2, in_1[3], in_2[1]);
  and and_29 (_4_3, in_1[3], in_2[2]);
  and and_30 (_5_3, in_1[4], in_2[2]);
  and and_31 (_5_4, in_1[4], in_2[3]);
  and and_32 (_4_4, in_1[3], in_2[3]);
  and and_33 (_4_5, in_1[3], in_2[4]);
  and and_34 (_5_5, in_1[4], in_2[4]);
  and and_35 (_5_6, in_1[4], in_2[5]);
  and and_36 (_4_6, in_1[3], in_2[5]);
  and and_37 (_4_7, in_1[3], in_2[6]);
  and and_38 (_5_7, in_1[4], in_2[6]);
  and and_39 (_5_8, in_1[4], in_2[7]);
  and and_40 (_4_8, in_1[3], in_2[7]);
  and and_41 (out_3[0], in_1[0], in_2[0]);
  and and_42 (_3_1, in_1[2], in_2[0]);
  and and_43 (_2_1, in_1[1], in_2[0]);
  and and_44 (_1_2, in_1[0], in_2[1]);
  and and_45 (_2_2, in_1[1], in_2[1]);
  and and_46 (_3_2, in_1[2], in_2[1]);
  and and_47 (_3_3, in_1[2], in_2[2]);
  and and_48 (_1_3, in_1[0], in_2[2]);
  and and_49 (_2_3, in_1[1], in_2[2]);
  and and_50 (_2_4, in_1[1], in_2[3]);
  and and_51 (_1_4, in_1[0], in_2[3]);
  and and_52 (_3_4, in_1[2], in_2[3]);
  and and_53 (_3_5, in_1[2], in_2[4]);
  and and_54 (_1_5, in_1[0], in_2[4]);
  and and_55 (_2_5, in_1[1], in_2[4]);
  and and_56 (_3_6, in_1[2], in_2[5]);
  and and_57 (_2_6, in_1[1], in_2[5]);
  and and_58 (_1_6, in_1[0], in_2[5]);
  and and_59 (_1_7, in_1[0], in_2[6]);
  and and_60 (_3_7, in_1[2], in_2[6]);
  and and_61 (_2_7, in_1[1], in_2[6]);
  and and_62 (_2_8, in_1[1], in_2[7]);
  and and_63 (_3_8, in_1[2], in_2[7]);
  and and_64 (_1_8, in_1[0], in_2[7]);

  // Other names for the same wires on the sheet: _1_1 = out_3[0]
endmodule

module SumToMult_2 (
  input  A,
  input  B,
  output S,
  output Cout
);

  xor xor_1 (S, A, B);
  and and_1 (Cout, A, B);
endmodule

module SumToMult (
  input  A,
  input  B,
  input  C,
  output Cout,
  output S
);

  wire and_1_out, and_2_out, and_3_out, xor_1_out;

  and and_1 (and_1_out, A, B);
  and and_2 (and_2_out, B, C);
  and and_3 (and_3_out, C, A);
  xor xor_1 (xor_1_out, A, B);
  xor xor_2 (S, xor_1_out, C);
  or or_1 (Cout, and_1_out, and_2_out, and_3_out);
endmodule

module main_2 (
  input  [7:0] A,
  input  [7:0] B,
  input  [2:0] Op
);

  wire [15:0] main_1_s;

  main main_1 (.A(A), .B(B), .Operation(Op), .S(main_1_s));
  Hex_Digit_Display hex_digit_display_1 (.value(main_1_s[15:12]));  // open: dp
  Hex_Digit_Display hex_digit_display_2 (.value(main_1_s[11:8]));  // open: dp
  Hex_Digit_Display hex_digit_display_3 (.value(main_1_s[7:4]));  // open: dp
  Hex_Digit_Display hex_digit_display_4 (.value(main_1_s[3:0]));  // open: dp

  // Notes on the sheet:
  //   000 - AND
  //   001 - OR
  //   010 - NOT(A)
  //   011 - Soma
  //   100 - Subtracao
  //   101 - DIvisao
  //   110 - Resto
  //   111 - Multiplicacao
endmodule
